// Logisim project address_decode_v2.circ as structural Verilog: 1 circuit, main circuit main
module main (
  output nODDROMCS,
  output nEVENROMCS,
  output nODDRAMCS,
  output nEVENRAMCS,
  output nBERR,
  output nIOSEL
);

  wire and_1_out, nand_1_out, not_1_out, or_1_out, or_2_out, or_3_out;

  not not_1 (not_1_out, 1'b0);
  and and_1 (and_1_out, 1'b0, 1'b1);
  or or_1 (or_1_out, 1'b0, 1'b0);
  or or_2 (or_2_out, not_1_out, 1'b0);
  or or_3 (or_3_out, not_1_out, 1'b0);
  or or_4 (nODDRAMCS, or_2_out, and_1_out);
  or or_5 (nEVENRAMCS, or_3_out, and_1_out);
  or or_6 (nODDROMCS, 1'b0, or_1_out);
  or or_7 (nEVENROMCS, or_1_out, 1'b0);
  not not_2 (nBERR, and_1_out);
  nand nand_1 (nand_1_out, nEVENRAMCS, nODDRAMCS, nEVENROMCS, nODDROMCS);
  or or_8 (nIOSEL, nand_1_out, and_1_out);

  // Notes on the sheet:
  //   /UDS
  //   /LDS
  //   Roscom68k Address Decoder version 1
  //   0x180000 - 0xFFFFFF - Unmapped (BERR)
  //   0x0 - 0x3FFFF - ROM (256Kb)
  //   0x40000 - 0x7FFFF - IO (256Kb)
  //   0x80000 - 0x17FFFF - RAM (1MB)
endmodule
