// Logisim project dtack_generator.circ as structural Verilog: 1 circuit, main circuit main
module main (
  input  nAS,
  input  nODDROMSEL,
  input  nEVENROMSEL,
  input  nODDRAMSEL,
  input  nEVENRAMSEL,
  input  nIOSEL,
  input  nMFPDTACK,
  output nDTACK
);

  wire and_1_out, and_2_out, and_3_out, and_4_out, or_1_out;

  and and_1 (and_1_out, nODDROMSEL, nEVENROMSEL);
  and and_2 (and_2_out, nODDRAMSEL, nEVENRAMSEL);
  or or_1 (or_1_out, nIOSEL, nMFPDTACK);
  and and_3 (and_3_out, and_1_out, and_2_out);
  and and_4 (and_4_out, and_3_out, or_1_out);
  or or_2 (nDTACK, nAS, and_4_out);
endmodule
