// Logisim project dtack_generator_v2.circ as structural Verilog: 1 circuit, main circuit main
module main (
  input  nODDROMCS,
  input  nEVENROMCS,
  input  nODDRAMCS,
  input  nODDRAMCS_2,
  input  nIACK,
  input  nIOSEL,
  input  nIODTACK,
  input  nLDS,
  input  nIACK_2,
  output nDTACK,
  output nDS
);

  wire and_1_out, and_3_out, not_1_out, or_1_out, or_2_out;

  and and_1 (and_1_out, nIACK, nIOSEL);
  and and_2 (nDS, nLDS, nIACK_2);
  and and_3 (and_3_out, nODDROMCS, nEVENROMCS, nODDRAMCS, nODDRAMCS_2);
  not not_1 (not_1_out, nIACK);
  or or_1 (or_1_out, and_1_out, nIODTACK);
  or or_2 (or_2_out, and_3_out, not_1_out);
  and and_4 (nDTACK, or_2_out, or_1_out);
endmodule
