// Logisim project address_decode_v1.circ as structural Verilog: 1 circuit, main circuit main
module main (
  input  nUDS,
  input  nLDS,
  input  nBOOT,
  output nODDRAMCS,
  output nEVENRAMCS,
  output nODDROMCS,
  output nEVENROMCS,
  output nIOSEL,
  output nEXPANSIONSEL
);

  wire and_1_out, and_2_out, and_5_out, nand_1_out, not_1_out, or_1_out, or_2_out, or_3_out, or_4_out,
       or_5_out, or_6_out, or_7_out, or_8_out;

  or or_1 (or_1_out, 1'b0, 1'b0);
  or or_2 (or_2_out, 1'b0, 1'b0);
  and and_1 (and_1_out, 1'b0, 1'b0, 1'b0, 1'b0);
  or or_3 (or_3_out, or_1_out, or_2_out);
  and and_2 (and_2_out, 1'b0, and_1_out);
  not not_1 (not_1_out, 1'b0);
  nand nand_1 (nand_1_out, 1'b0, and_2_out);
  nand nand_2 (nIOSEL, not_1_out, and_1_out);
  or or_4 (or_4_out, or_3_out, nBOOT);
  or or_5 (or_5_out, or_3_out, nUDS);
  or or_6 (or_6_out, nLDS, or_3_out);
  or or_7 (or_7_out, nand_1_out, nUDS);
  or or_8 (or_8_out, nLDS, nand_1_out);
  and and_3 (nODDROMCS, or_7_out, or_4_out);
  and and_4 (nEVENROMCS, or_8_out, or_4_out);
  xnor xnor_1 (nODDRAMCS, or_5_out, or_4_out);
  xnor xnor_2 (nEVENRAMCS, or_6_out, or_4_out);
  and and_5 (and_5_out, nIOSEL, nEVENROMCS, nODDROMCS, nEVENRAMCS);
  nand nand_3 (nEXPANSIONSEL, and_5_out, nODDRAMCS);

  // Notes on the sheet:
  //   Roscom68k Address Decoder version 1
  //   0x000000 - 0x0FFFFF - RAM (1MB)
  //   0x100000 - 0xF7FFFF - Expansion RAM
  //   0xF80000 - 0xFBFFFF - IO (256KB) 
  //   0xFC0000 - 0xFFFFFF - ROM (256KB)
endmodule
